// Logisim project CPU.circ as structural Verilog: 16 circuits, main circuit main
module main (
  input  [2:0] Program__sum_max_iter_rec,
  input  CLR
);

  wire ALUSrc, and_1_out, BL, BX, CLK, comparator_1_eq, control_unit_1_regwrite, MemToReg, MemWrite, PCSrc;
  wire [1:0] control_unit_1_regsrc, ImmSrc;
  wire [2:0] ALUControl;
  wire [3:0] A3, ALUFlags, multiplexer_2_out, multiplexer_4_out, Rm;
  wire [4:0] Shift;
  wire [31:0] adder_1_out, adder_2_out, alu_1_aluresult, data_memory_1_rd, extend_immediate_1_out, Instr,
       multiplexer_1_out, multiplexer_3_out, multiplexer_7_out, multiplexer_8_out, PC, register_file_1_r0,
       register_file_1_r1, register_file_1_r2, register_file_1_r3, register_file_1_r4,
       register_file_1_r13_sp, register_file_1_r14_lr, register_file_1_rd1, register_file_1_rd2,
       shifter_1_out;

  Clock u_CLK (.out(CLK));
  // Probe on multiplexer_1_out
  Multiplexer #(.width(32), .enable("false")) multiplexer_1 (
    .in0(adder_1_out), .in1(multiplexer_8_out), .out(multiplexer_1_out), .sel(PCSrc));
  Comparator #(.width(32)) comparator_1 (.a(multiplexer_8_out), .b(PC), .eq(comparator_1_eq));  // open: gt, lt
  // Probe on ALUFlags
  Register #(.width(32)) register_1 (.D(multiplexer_1_out), .en(1'b1), .Q(PC), .clk(CLK));  // open: clr
  // Probe on PC
  Adder #(.width(32)) adder_1 (.a(PC), .b(32'h4), .out(adder_1_out), .cin(1'b0));  // open: cout
  and and_1 (and_1_out, comparator_1_eq, PCSrc);
  LED Green___running___Red___stopped (.in(and_1_out));
  Control_Unit control_unit_1 (
    .ALUFlags(ALUFlags), .Instr(Instr), .PCSrc(PCSrc), .RegWrite(control_unit_1_regwrite),
    .MemWrite(MemWrite), .MemToReg(MemToReg), .ALUSrc(ALUSrc), .ImmSrc(ImmSrc),
    .RegSrc(control_unit_1_regsrc), .ALUControl(ALUControl), .CLK(CLK), .Branch_and_Link(BL), .BX(BX));
  // Probe on Instr
  Instruction_Memory instruction_memory_1 (.PC(PC), .Instr(Instr), .File__sum_max_iter_rec(Program__sum_max_iter_rec));
  Multiplexer #(.width(4), .enable("false")) multiplexer_2 (
    .in0(Rm), .in1(Instr[15:12]), .out(multiplexer_2_out), .sel(control_unit_1_regsrc[1]));
  // Probe on multiplexer_3_out
  Multiplexer #(.width(32), .enable("false")) multiplexer_3 (
    .in0(multiplexer_8_out), .in1(adder_1_out), .out(multiplexer_3_out), .sel(BL));
  // Probe on register_file_1_r0
  BitSelector #(.width(32), .group(4)) bitselector_1 (.in(Instr), .out(Rm), .sel(3'b000));
  Multiplexer #(.width(4), .enable("false")) multiplexer_4 (
    .in0(Instr[19:16]), .in1(4'b1111), .out(multiplexer_4_out), .sel(control_unit_1_regsrc[0]));
  Adder #(.width(32)) adder_2 (.a(adder_1_out), .b(32'h4), .out(adder_2_out), .cin(1'b0));  // open: cout
  // Probe on register_file_1_r1
  // Probe on A3
  Multiplexer #(.width(4), .enable("false")) multiplexer_5 (.in0(Instr[15:12]), .in1(4'b1110), .out(A3), .sel(BL));
  Multiplexer #(.width(5), .enable("false")) multiplexer_6 (.in0(Instr[9:5]), .in1({5{1'b0}}), .out(Shift), .sel(BX));
  Extend_Immediate extend_immediate_1 (.in(Instr), .out(extend_immediate_1_out), .ImmSrc(ImmSrc));
  // Probe on register_file_1_r14_lr
  // Probe on register_file_1_r13_sp
  // Probe on register_file_1_rd1
  Register_File register_file_1 (
    .A1(multiplexer_4_out), .A2(multiplexer_2_out), .A3(A3), .R15_in(adder_2_out), .RD1(register_file_1_rd1),
    .RD2(register_file_1_rd2), .WD3(multiplexer_3_out), .CLK(CLK), .CLR(CLR), .WE3(control_unit_1_regwrite),
    .R0(register_file_1_r0), .R1(register_file_1_r1), .R2(register_file_1_r2), .R3(register_file_1_r3),
    .R4(register_file_1_r4), .R13_SP(register_file_1_r13_sp), .R14_LR(register_file_1_r14_lr));  // open: R15_out, R5, R6, R7
  // Probe on extend_immediate_1_out
  // Probe on register_file_1_r2
  Shifter #(.width(32)) shifter_1 (.in(register_file_1_rd2), .\dist (Shift), .out(shifter_1_out));
  // Probe on register_file_1_r3
  // Probe on multiplexer_7_out
  Multiplexer #(.width(32), .enable("false")) multiplexer_7 (
    .in0(shifter_1_out), .in1(extend_immediate_1_out), .out(multiplexer_7_out), .sel(ALUSrc));
  // Probe on ALUControl
  ALU alu_1 (
    .ALUResult(alu_1_aluresult), .ALUFlags(ALUFlags), .ALUControl(ALUControl), .A(register_file_1_rd1),
    .B(multiplexer_7_out));
  // Probe on register_file_1_rd2
  // Probe on register_file_1_r4
  // Probe on alu_1_aluresult
  Data_Memory data_memory_1 (
    .A(alu_1_aluresult), .CLK(CLK), .CLR(CLR), .WE(MemWrite), .WD(register_file_1_rd2), .RD(data_memory_1_rd));
  // Probe on data_memory_1_rd
  Multiplexer #(.width(32), .enable("false")) multiplexer_8 (
    .in0(alu_1_aluresult), .in1(data_memory_1_rd), .out(multiplexer_8_out), .sel(MemToReg));

  // Other names for the same wires on the sheet: Instr_imm12[11:0] = Instr[11:0]; Rd[3:0] = Instr[15:12];
  //   Rn[3:0] = Instr[19:16]
endmodule

module ALU_Decoder (
  input  [5:0] Funct,
  input  AluOp,
  output [2:0] ALUControl,
  output [1:0] FlagW,
  output NoWrite
);

  wire and_1_out, comparator_1_eq;

  // Probe on Funct[4:1]
  and and_1 (and_1_out, Funct[0], AluOp);
  Comparator #(.width(4)) comparator_1 (.a(Funct[4:1]), .b(4'b1010), .eq(comparator_1_eq));  // open: gt, lt
  and and_2 (NoWrite, comparator_1_eq, AluOp);
  Multiplexer #(.select(4), .width(3), .enable("false")) multiplexer_1 (
    .in0(3'b010), .in2(3'b001), .in4(3'b000), .in7(3'b000), .in8(3'b000), .in9(3'b100), .in10(3'b001),
    .in12(3'b011), .in13(3'b100), .in14(3'b100), .in15(3'b101), .out(ALUControl), .sel(Funct[4:1]));  // open: in1, in3, in5, in6, in11
  Multiplexer #(.width(2), .enable("false")) multiplexer_2 (.in0(2'b00), .in1(2'b11), .out(FlagW), .sel(and_1_out));

  // Notes on the sheet:
  //   S
endmodule

module Register_File (
  input  CLK,
  input  CLR,
  input  WE3,
  input  [31:0] WD3,
  input  [3:0] A1,
  input  [3:0] A3,
  input  [3:0] A2,
  input  [31:0] R15_in,
  output [31:0] RD1,
  output [31:0] RD2,
  output [31:0] R15_out,
  output [31:0] R0,
  output [31:0] R1,
  output [31:0] R2,
  output [31:0] R3,
  output [31:0] R14_LR,
  output [31:0] R4,
  output [31:0] R5,
  output [31:0] R6,
  output [31:0] R7,
  output [31:0] R13_SP
);

  wire decoder_1_out0, decoder_1_out1, decoder_1_out2, decoder_1_out3, decoder_1_out4, decoder_1_out5,
       decoder_1_out6, decoder_1_out7, decoder_1_out8, decoder_1_out9, decoder_1_out10, decoder_1_out11,
       decoder_1_out12, decoder_1_out13, decoder_1_out14, decoder_1_out15, en0_out, en1_out, en2_out,
       en3_out, en4_out, en5_out, en6_out, en7_out, en8_out, en9_out, en10_out, en11_out, en12_out, en13_out,
       en14_out;
  wire [31:0] R8, R9_q, R10_q, R11_q, R12_q;

  Decoder_part #(.select(4)) decoder_1 (
    .out0(decoder_1_out0), .out1(decoder_1_out1), .out2(decoder_1_out2), .out3(decoder_1_out3),
    .out4(decoder_1_out4), .out5(decoder_1_out5), .out6(decoder_1_out6), .out7(decoder_1_out7),
    .out8(decoder_1_out8), .out9(decoder_1_out9), .out10(decoder_1_out10), .out11(decoder_1_out11),
    .out12(decoder_1_out12), .out13(decoder_1_out13), .out14(decoder_1_out14), .out15(decoder_1_out15),
    .sel(A3));  // open: en
  and en0 (en0_out, WE3, decoder_1_out0);
  and en1 (en1_out, WE3, decoder_1_out1);
  and en2 (en2_out, WE3, decoder_1_out2);
  and en3 (en3_out, WE3, decoder_1_out3);
  and en4 (en4_out, WE3, decoder_1_out4);
  and en5 (en5_out, WE3, decoder_1_out5);
  and en6 (en6_out, WE3, decoder_1_out6);
  and en7 (en7_out, WE3, decoder_1_out7);
  and en8 (en8_out, WE3, decoder_1_out8);
  and en9 (en9_out, WE3, decoder_1_out9);
  and en10 (en10_out, WE3, decoder_1_out10);
  and en11 (en11_out, WE3, decoder_1_out11);
  and en12 (en12_out, WE3, decoder_1_out12);
  and en13 (en13_out, WE3, decoder_1_out13);
  and en14 (en14_out, WE3, decoder_1_out14);
  Register #(.width(32)) u_R0 (.D(WD3), .en(en0_out), .Q(R0), .clk(CLK), .clr(CLR));
  Register #(.width(32)) u_R1 (.D(WD3), .en(en1_out), .Q(R1), .clk(CLK), .clr(CLR));
  Register #(.width(32)) u_R2 (.D(WD3), .en(en2_out), .Q(R2), .clk(CLK), .clr(CLR));
  Register #(.width(32)) u_R3 (.D(WD3), .en(en3_out), .Q(R3), .clk(CLK), .clr(CLR));
  Register #(.width(32)) u_R4 (.D(WD3), .en(en4_out), .Q(R4), .clk(CLK), .clr(CLR));
  Register #(.width(32)) u_R5 (.D(WD3), .en(en5_out), .Q(R5), .clk(CLK), .clr(CLR));
  Register #(.width(32)) u_R6 (.D(WD3), .en(en6_out), .Q(R6), .clk(CLK), .clr(CLR));
  Register #(.width(32)) u_R7 (.D(WD3), .en(en7_out), .Q(R7), .clk(CLK), .clr(CLR));
  Register #(.width(32)) u_R8 (.D(WD3), .en(en8_out), .Q(R8), .clk(CLK), .clr(CLR));
  Register #(.width(32)) R9 (.D(WD3), .en(en9_out), .Q(R9_q), .clk(CLK), .clr(CLR));
  Register #(.width(32)) R10 (.D(WD3), .en(en10_out), .Q(R10_q), .clk(CLK), .clr(CLR));
  Register #(.width(32)) R11 (.D(WD3), .en(en11_out), .Q(R11_q), .clk(CLK), .clr(CLR));
  Register #(.width(32)) R12 (.D(WD3), .en(en12_out), .Q(R12_q), .clk(CLK), .clr(CLR));
  Register #(.width(32)) R13 (.D(WD3), .en(en13_out), .Q(R13_SP), .clk(CLK), .clr(CLR));
  Register #(.width(32)) R14 (.D(WD3), .en(en14_out), .Q(R14_LR), .clk(CLK), .clr(CLR));
  Multiplexer #(.select(4), .width(32)) multiplexer_1 (
    .in0(R0), .in1(R1), .in2(R2), .in3(R3), .in4(R4), .in5(R5), .in6(R6), .in7(R7), .in8(R8), .in9(R9_q),
    .in10(R10_q), .in11(R11_q), .in12(R12_q), .in13(R13_SP), .in14(R14_LR), .in15(R15_in), .out(RD1), .sel(A1));  // open: en
  Multiplexer #(.select(4), .width(32)) multiplexer_2 (
    .in0(R0), .in1(R1), .in2(R2), .in3(R3), .in4(R4), .in5(R5), .in6(R6), .in7(R7), .in8(R8), .in9(R9_q),
    .in10(R10_q), .in11(R11_q), .in12(R12_q), .in13(R13_SP), .in14(R14_LR), .in15(R15_in), .out(RD2), .sel(A2));  // open: en

  assign R15_out = R15_in;
endmodule

module Data_Memory (
  input  [31:0] A,
  input  CLK,
  input  CLR,
  input  WE,
  input  [31:0] WD,
  output [31:0] RD
);

  wire not_1_out;
  wire [7:0] bitselector_1_out;

  BitSelector #(.width(32), .group(8)) bitselector_1 (.in(A), .out(bitselector_1_out), .sel(2'b00));
  RAM #(.dataWidth(32), .bus("separate")) ram_1 (
    .addr(bitselector_1_out), .din(WD), .data(RD), .str(WE), .clk(CLK), .ld(not_1_out), .clr(CLR));  // open: sel
  not not_1 (not_1_out, WE);
endmodule

module Instruction_Memory (
  input  [31:0] PC,
  input  [2:0] File__sum_max_iter_rec,
  output [31:0] Instr
);

  wire [7:0] bitselector_1_out, shifter_1_out;
  wire [31:0] rom_1_data, rom_2_data, rom_3_data, rom_4_data, rom_5_data;

  BitSelector #(.width(32), .group(8)) bitselector_1 (.in(PC), .out(bitselector_1_out), .sel(2'b00));
  Shifter #(.shift("lr")) shifter_1 (.in(bitselector_1_out), .\dist (3'b010), .out(shifter_1_out));
  ROM #(.dataWidth(32)) rom_1 (.addr(shifter_1_out), .data(rom_1_data));  // open: sel
  ROM #(.dataWidth(32)) rom_2 (.addr(shifter_1_out), .data(rom_2_data));  // open: sel
  ROM #(.dataWidth(32)) rom_3 (.addr(shifter_1_out), .data(rom_3_data));  // open: sel
  ROM #(.dataWidth(32)) rom_4 (.addr(shifter_1_out), .data(rom_4_data));  // open: sel
  ROM #(.dataWidth(32)) rom_5 (.addr(shifter_1_out), .data(rom_5_data));  // open: sel
  Multiplexer #(.select(3), .width(32), .disabled(0), .enable("false")) multiplexer_1 (
    .in0(rom_1_data), .in1(rom_2_data), .in2(rom_3_data), .in3(rom_4_data), .in4(rom_5_data), .out(Instr),
    .sel(File__sum_max_iter_rec));  // open: in5, in6, in7

  // Notes on the sheet:
  //   find_max
  //   fib_iter
  //   fib_rec
  //   add_bxlr
  //   sum_array
  //   contents of rom_1 (hex, n*v repeats v):
  //   e3a0d07c e08dd00d e24dd004 e3a00009 e58d0000 e24dd004 e3a00038 e58d0000 e24dd004 e3a00007 e58d0000
  //   e24dd004 e3a00006 e58d0000 e24dd004 e3a00005 e58d0000 e24dd004 e3a00004 e58d0000 e24dd004 e3a00003
  //   e58d0000 e24dd004 e3a00002 e58d0000 e24dd004 e3a00001 e58d0000 e1a0000d e3a01009 eb000001 eaffffff
  //   eafffffe e24dd008 e58d4000 e5904000 e1a02004 e3a03000 e3510001 a00000d e1530001 a00000b e1540002
  //   a1a02004 e2833001 e1530001 a000006 e1a05000 e1a06003 e0866006 e0866006 e0855006 e5954000 eafffff1
  //   e59d4000 e28dd008 e1a00002 e1a0f00e
  //   contents of rom_2 (hex, n*v repeats v):
  //   e3a0d07c e08dd00d e24dd004 e3a00001 e58d0000 e24dd004 e3a00002 e58d0000 e24dd004 e3a00003 e58d0000
  //   e24dd004 e3a00004 e58d0000 e24dd004 e3a00005 e58d0000 e24dd004 e3a00006 e58d0000 e24dd004 e3a00007
  //   e58d0000 e24dd004 e3a00008 e58d0000 e24dd004 e3a00009 e58d0000 e1a0000d e3a01009 eb000003 e3a04000
  //   e2444001 eaffffff eafffffe e3a02000 e3a03000 e3510000 a000005 e5904000 e2800004 e0822004 e2833001
  //   e1530001 1afffff9 e1a00002 e1a0f00e
  //   contents of rom_3 (hex, n*v repeats v):
  //   e3a0d07c e08dd00d e3a0000a eb000001 eaffffff eafffffe e3500000 1a0f00e e3500001 1a0f00e e2801001
  //   e1a02001 e0822002 e0822002 e04dd002 e3a02000 e58d2000 e3a02001 e1a0800d e2888004 e5882000 e3a02001
  //   e2888004 e5882000 e3a03002 e2833001 e1530001 a000012 e2432001 e1a08002 e0888008 e0888008 e088800d
  //   e5984000 e2432002 e1a08002 e0888008 e0888008 e088800d e5985000 e0844005 e1a08003 e0888008 e0888008
  //   e088800d e5884000 eaffffe9 e0800000 e0800000 e080100d e5910000 e0811001 e0811001 e08dd001 e1a0f00e
  //   contents of rom_4 (hex, n*v repeats v):
  //   e3a0d07c e08dd00d e3a0000a eb000001 eaffffff eafffffe e3500000 1a0f00e e3500001 1a0f00e e1a01000
  //   e24dd010 e58d1000 e28d8008 e588e000 e2400001 ebfffff4 e1a02000 e59d1000 e28d8004 e5882000 e2410002
  //   ebffffee e28d8004 e5981000 e2888004 e598e000 e28dd010 e0800001 e1a0f00e
  //   contents of rom_5 (hex, n*v repeats v):
  //   e3a00002 e3a01003 eb000000 ea000001 e0800001 e12fff1e eafffffe
endmodule

module Main_Decoder (
  input  [1:0] Op,
  input  [5:0] Funct,
  input  BX,
  output [1:0] ImmSrc,
  output MemToReg,
  output MemW,
  output ALUSrc,
  output RegW,
  output [1:0] RegSrc,
  output ALUOp,
  output Branch,
  output Branch_and_Link
);

  wire and_3_out, and_4_out, and_6_out, and_8_out;

  and and_1 (MemToReg, ~Op[1], Op[0], Funct[0]);  // AND_Gate
  and and_2 (MemW, ~Op[1], Op[0], ~Funct[0]);  // AND_Gate
  nand nand_1 (ALUSrc, ~Op[1], ~Op[0], ~Funct[5]);  // NAND_Gate
  and and_3 (and_3_out, ~Op[1], ~Op[0]);  // AND_Gate
  and and_4 (and_4_out, ~Op[1], Op[0], Funct[0]);  // AND_Gate
  and and_5 (RegSrc[1], ~Op[1], Op[0]);  // AND_Gate
  and and_6 (and_6_out, Op[1], ~Op[0]);  // AND_Gate
  and and_7 (ALUOp, ~Op[1], ~BX, ~Op[0]);  // AND_Gate
  and and_8 (and_8_out, Op[1], ~Op[0]);  // AND_Gate
  or or_1 (RegW, and_3_out, BX, and_4_out);
  or or_2 (RegSrc[0], BX, and_6_out);
  or or_3 (Branch, BX, and_8_out);
  and and_9 (Branch_and_Link, and_8_out, Funct[4]);

  assign ImmSrc = Op;
endmodule

module Extend_Immediate (
  input  [31:0] in,
  input  [1:0] ImmSrc,
  output [31:0] out
);

  wire [7:0] bitselector_1_out;
  wire [11:0] bitselector_2_out;
  wire [23:0] bitselector_3_out;
  wire [31:0] bit_extender_1_out, bit_extender_2_out, bit_extender_3_out, shifter_1_out;

  BitSelector #(.width(32), .group(8)) bitselector_1 (.in(in), .out(bitselector_1_out), .sel(2'b00));
  BitSelector #(.width(32), .group(12)) bitselector_2 (.in(in), .out(bitselector_2_out), .sel(2'b00));
  BitSelector #(.width(32), .group(24)) bitselector_3 (.in(shifter_1_out), .out(bitselector_3_out), .sel(1'b0));
  Shifter #(.width(32)) shifter_1 (.in(in), .\dist (5'b00010), .out(shifter_1_out));
  assign bit_extender_1_out = {{24{1'b0}}, bitselector_1_out};  // Bit_Extender bit_extender_1
  assign bit_extender_2_out = {{20{1'b0}}, bitselector_2_out};  // Bit_Extender bit_extender_2
  assign bit_extender_3_out = {{8{bitselector_3_out[23]}}, bitselector_3_out};  // Bit_Extender bit_extender_3
  Multiplexer #(.select(2), .width(32), .enable("false")) multiplexer_1 (
    .in0(bit_extender_1_out), .in1(bit_extender_2_out), .in2(bit_extender_3_out), .out(out), .sel(ImmSrc));  // open: in3
endmodule

module ALU (
  input  [2:0] ALUControl,
  input  [31:0] A,
  input  [31:0] B,
  output [31:0] ALUResult,
  output [3:0] ALUFlags
);

  wire adder_1_cout, most_significant_bit_1_msb, most_significant_bit_2_msb, multiplexer_2_out,
       subtractor_1_bout, xnor_1_out, xor_1_out;
  wire [31:0] adder_1_out, and_1_out, multiplexer_1_out, not_1_out, or_1_out, subtractor_1_out;

  Most_Significant_Bit most_significant_bit_1 (.in(A), .msb(most_significant_bit_1_msb));
  Most_Significant_Bit most_significant_bit_2 (.in(B), .msb(most_significant_bit_2_msb));
  Subtractor #(.width(32)) subtractor_1 (.a(A), .b(B), .out(subtractor_1_out), .bin(1'b0), .bout(subtractor_1_bout));
  Adder #(.width(32)) adder_1 (.a(A), .b(B), .out(adder_1_out), .cin(1'b0), .cout(adder_1_cout));
  assign or_1_out = A | B;  // OR_Gate or_1, 32 bits wide
  NotExactlyOne xnor_1 (
    .out(xnor_1_out), .in0(most_significant_bit_2_msb), .in1(most_significant_bit_1_msb), .in2(ALUControl[0]));
  Multiplexer #(.width(32), .enable("false")) multiplexer_1 (
    .in0(adder_1_out), .in1(subtractor_1_out), .out(multiplexer_1_out), .sel(ALUControl[0]));
  assign and_1_out = A & B;  // AND_Gate and_1, 32 bits wide
  Comparator #(.width(32)) comparator_1 (.a(subtractor_1_out), .b({32{1'b0}}));  // open: gt, eq, lt
  assign not_1_out = ~B;  // NOT_Gate not_1, 32 bits wide
  Multiplexer #(.enable("false")) multiplexer_2 (
    .in0(adder_1_cout), .in1(subtractor_1_bout), .out(multiplexer_2_out), .sel(ALUControl[0]));
  Multiplexer #(.select(3), .width(32), .disabled(0), .enable("false")) multiplexer_3 (
    .in0(multiplexer_1_out), .in1(multiplexer_1_out), .in2(and_1_out), .in3(or_1_out), .in4(B),
    .in5(not_1_out), .in6({32{1'b0}}), .in7({32{1'b0}}), .out(ALUResult), .sel(ALUControl));
  and and_2 (ALUFlags[1], multiplexer_2_out, ~ALUControl[1]);  // AND_Gate
  Comparator #(.width(32)) comparator_2 (.a(ALUResult), .b({32{1'b0}}), .eq(ALUFlags[2]));  // open: gt, lt
  Most_Significant_Bit most_significant_bit_3 (.in(ALUResult), .msb(ALUFlags[3]));
  xor xor_1 (xor_1_out, ALUFlags[3], most_significant_bit_1_msb);
  and and_3 (ALUFlags[0], xor_1_out, ~ALUControl[1], xnor_1_out);  // AND_Gate

  // Notes on the sheet:
  //   A31
  //   B31
  //   V
  //   C
  //   Z
  //   N
endmodule

module Most_Significant_Bit (
  input  [31:0] in,
  output msb
);


  assign msb = in[31];
endmodule

module Control_Unit (
  input  CLK,
  input  [3:0] ALUFlags,
  input  [31:0] Instr,
  output PCSrc,
  output RegWrite,
  output MemWrite,
  output MemToReg,
  output ALUSrc,
  output Branch_and_Link,
  output [1:0] ImmSrc,
  output [1:0] RegSrc,
  output [2:0] ALUControl,
  output BX
);

  wire decoder_1_memw, decoder_1_nowrite, decoder_1_pcs, decoder_1_regw;
  wire [1:0] decoder_1_flagw;

  // Probe on Instr[15:12]
  // Probe on Instr[27:26]
  // Probe on Instr[25:20]
  Decoder decoder_1 (
    .Rd(Instr[15:12]), .Op(Instr[27:26]), .Funct(Instr[25:20]), .PCS(decoder_1_pcs), .RegW(decoder_1_regw),
    .MemW(decoder_1_memw), .MemToReg(MemToReg), .ALUSrc(ALUSrc), .ImmSrc(ImmSrc), .RegSrc(RegSrc),
    .NoWrite(decoder_1_nowrite), .ALUControl(ALUControl), .FlagW(decoder_1_flagw),
    .Branch_and_Link(Branch_and_Link));
  Conditional_Logic conditional_logic_1 (
    .PCS(decoder_1_pcs), .RegW(decoder_1_regw), .MemW(decoder_1_memw), .FlagW(decoder_1_flagw), .CLK(CLK),
    .Cond(Instr[31:28]), .ALUFlags(ALUFlags), .PCSrc(PCSrc), .RegWrite(RegWrite), .MemWrite(MemWrite),
    .NoWrite(decoder_1_nowrite), .BL(Branch_and_Link));
  BX_check bx_check_1 (.Op(Instr[27:26]), .Funct(Instr[25:20]), .isBx(BX));

  // Other names for the same wires on the sheet: Rd[3:0] = Instr[15:12]; Funct[5:0] = Instr[25:20];
  //   Op[1:0] = Instr[27:26]; Cond[3:0] = Instr[31:28]
endmodule

module Decoder (
  input  [3:0] Rd,
  input  [1:0] Op,
  input  [5:0] Funct,
  output PCS,
  output RegW,
  output MemW,
  output MemToReg,
  output ALUSrc,
  output [1:0] ImmSrc,
  output [1:0] RegSrc,
  output Branch_and_Link,
  output NoWrite,
  output [1:0] FlagW,
  output [2:0] ALUControl
);

  wire branch_check_1_branch, bx_check_1_isbx, main_decoder_1_aluop, main_decoder_1_branch;
  wire [2:0] alu_decoder_1_alucontrol;

  Branch_Check branch_check_1 (.Op(Op), .Funct(Funct), .Branch(branch_check_1_branch));
  BX_check bx_check_1 (.Op(Op), .Funct(Funct), .isBx(bx_check_1_isbx));
  PC_Logic pc_logic_1 (.Branch(main_decoder_1_branch), .RegW(RegW), .Rd(Rd), .PCS(PCS));
  Main_Decoder main_decoder_1 (
    .ImmSrc(ImmSrc), .MemToReg(MemToReg), .MemW(MemW), .ALUSrc(ALUSrc), .RegW(RegW), .RegSrc(RegSrc),
    .ALUOp(main_decoder_1_aluop), .Branch(main_decoder_1_branch), .Op(Op), .Funct(Funct),
    .Branch_and_Link(Branch_and_Link), .BX(bx_check_1_isbx));
  ALU_Decoder alu_decoder_1 (
    .ALUControl(alu_decoder_1_alucontrol), .FlagW(FlagW), .NoWrite(NoWrite), .AluOp(main_decoder_1_aluop),
    .Funct(Funct));
  Multiplexer #(.width(3), .disabled(0), .enable("false")) multiplexer_1 (
    .in0(alu_decoder_1_alucontrol), .in1(3'b000), .out(ALUControl), .sel(branch_check_1_branch));
endmodule

module PC_Logic (
  input  Branch,
  input  RegW,
  input  [3:0] Rd,
  output PCS
);

  wire and_1_out, comparator_1_eq;

  Comparator #(.width(4)) comparator_1 (.a(Rd), .b(4'b1111), .eq(comparator_1_eq));  // open: gt, lt
  and and_1 (and_1_out, RegW, comparator_1_eq);
  or or_1 (PCS, Branch, and_1_out);
endmodule

module Condition_Check (
  input  [3:0] ALUFlags,
  input  [3:0] Cond,
  output CondEx
);

  wire and_1_out, and_2_out, not_1_out, not_2_out, not_3_out, not_4_out, or_1_out, or_2_out, xnor_1_out,
       xor_1_out;

  not not_1 (not_1_out, ALUFlags[1]);
  not not_2 (not_2_out, ALUFlags[2]);
  not not_3 (not_3_out, ALUFlags[3]);
  not not_4 (not_4_out, ALUFlags[0]);
  and and_1 (and_1_out, not_2_out, ALUFlags[1]);
  or or_1 (or_1_out, ALUFlags[2], not_1_out);
  xnor xnor_1 (xnor_1_out, ALUFlags[3], ALUFlags[0]);
  xor xor_1 (xor_1_out, ALUFlags[3], ALUFlags[0]);
  and and_2 (and_2_out, xnor_1_out, not_2_out);
  or or_2 (or_2_out, xor_1_out, ALUFlags[2]);
  Multiplexer #(.select(4), .enable("false")) multiplexer_1 (
    .in0(ALUFlags[2]), .in1(not_2_out), .in2(ALUFlags[1]), .in3(not_1_out), .in4(ALUFlags[3]),
    .in5(not_3_out), .in6(ALUFlags[0]), .in7(not_4_out), .in8(and_1_out), .in9(or_1_out), .in10(xnor_1_out),
    .in11(xor_1_out), .in12(and_2_out), .in13(or_2_out), .in14(1'b1), .out(CondEx), .sel(Cond));  // open: in15

  // Notes on the sheet:
  //   NZCV
endmodule

module Conditional_Logic (
  input  PCS,
  input  RegW,
  input  BL,
  input  NoWrite,
  input  [1:0] FlagW,
  input  MemW,
  input  CLK,
  input  [3:0] Cond,
  input  [3:0] ALUFlags,
  output PCSrc,
  output RegWrite,
  output MemWrite
);

  wire and_1_out, and_2_out, condition_check_1_condex, or_1_out;
  wire [1:0] register_1_q, register_2_q;

  Register #(.width(2)) register_1 (.D(ALUFlags[3:2]), .en(and_1_out), .Q(register_1_q), .clk(CLK));  // open: clr
  and and_1 (and_1_out, FlagW[1], condition_check_1_condex);
  Register #(.width(2)) register_2 (.D(ALUFlags[1:0]), .en(and_2_out), .Q(register_2_q), .clk(CLK));  // open: clr
  and and_2 (and_2_out, FlagW[0], condition_check_1_condex);
  or or_1 (or_1_out, RegW, BL);
  // Probe on {register_1_q, register_2_q}
  Condition_Check condition_check_1 (
    .ALUFlags({register_1_q, register_2_q}), .CondEx(condition_check_1_condex), .Cond(Cond));
  and and_3 (PCSrc, PCS, condition_check_1_condex);
  and and_4 (RegWrite, or_1_out, ~NoWrite, condition_check_1_condex);  // AND_Gate
  and and_5 (MemWrite, MemW, condition_check_1_condex);
endmodule

module Branch_Check (
  input  [1:0] Op,
  input  [5:0] Funct,
  output Branch
);

  wire comparator_1_eq;

  Comparator #(.width(2)) comparator_1 (.a(Op), .b(2'b10), .eq(comparator_1_eq));  // open: gt, lt
  and and_1 (Branch, comparator_1_eq, Funct[5]);
endmodule

module BX_check (
  input  [1:0] Op,
  input  [5:0] Funct,
  output isBx
);

  wire comparator_1_eq, comparator_2_eq;

  Comparator #(.width(2)) comparator_1 (.a(Op), .b(2'b00), .eq(comparator_1_eq));  // open: gt, lt
  Comparator #(.width(6)) comparator_2 (.a(Funct), .b(6'b010010), .eq(comparator_2_eq));  // open: gt, lt
  and and_1 (isBx, comparator_1_eq, comparator_2_eq);
endmodule
